// Logisim project traffic-light-system.circ as structural Verilog
module _4_bit_counter (
  input  Power,
  input  Zero,
  output out_3,
  output out_4,
  output out_5,
  output out_6
);

  wire and_1_out, and_2_out, clock_1_out;

  Clock clock_1 (.out(clock_1_out));
  J_K_Flip_Flop j_k_ff_1 (.J(Power), .clk(clock_1_out), .K(Power), .Q(out_3), .reset(Zero));  // open: Qn, preset, en
  and and_1 (and_1_out, out_3, out_4);
  J_K_Flip_Flop j_k_ff_2 (.J(out_3), .clk(clock_1_out), .K(out_3), .Q(out_4), .reset(Zero));  // open: Qn, preset, en
  J_K_Flip_Flop j_k_ff_3 (
    .J(and_1_out), .clk(clock_1_out), .K(and_1_out), .Q(out_5), .reset(Zero));  // open: Qn, preset, en
  and and_2 (and_2_out, and_1_out, out_5);
  J_K_Flip_Flop j_k_ff_4 (
    .J(and_2_out), .clk(clock_1_out), .K(and_2_out), .Q(out_6), .reset(Zero));  // open: Qn, preset, en

  // Notes on the sheet:
  //   Clock
endmodule
